// Logisim project additions.circ as structural Verilog
module regfile (
  input  [2:0] Read1,
  input  [2:0] Read2,
  input  [2:0] RegWrite,
  input  [7:0] WriteData,
  input  WE,
  input  Clock,
  input  Reset,
  output [7:0] ReadData1,
  output [7:0] ReadData2
);

  wire demultiplexer_1_out0, demultiplexer_1_out1, demultiplexer_1_out2, demultiplexer_1_out3,
       demultiplexer_1_out4, demultiplexer_1_out5, demultiplexer_1_out6, demultiplexer_1_out7;
  wire [7:0] register_1_q, register_2_q, register_3_q, register_4_q, register_5_q, register_6_q,
       register_7_q, register_8_q;

  Demultiplexer #(.select(3), .enable("false")) demultiplexer_1 (
    .out0(demultiplexer_1_out0), .out1(demultiplexer_1_out1), .out2(demultiplexer_1_out2),
    .out3(demultiplexer_1_out3), .out4(demultiplexer_1_out4), .out5(demultiplexer_1_out5),
    .out6(demultiplexer_1_out6), .out7(demultiplexer_1_out7), .in(WE), .sel(RegWrite));
  Register #(.trigger("falling")) register_1 (
    .D(WriteData), .en(demultiplexer_1_out0), .Q(register_1_q), .clk(Clock), .clr(Reset));
  Register #(.trigger("falling")) register_2 (
    .D(WriteData), .en(demultiplexer_1_out1), .Q(register_2_q), .clk(Clock), .clr(Reset));
  Register #(.trigger("falling")) register_3 (
    .D(WriteData), .en(demultiplexer_1_out2), .Q(register_3_q), .clk(Clock), .clr(Reset));
  Register #(.trigger("falling")) register_4 (
    .D(WriteData), .en(demultiplexer_1_out3), .Q(register_4_q), .clk(Clock), .clr(Reset));
  Register #(.trigger("falling")) register_5 (
    .D(WriteData), .en(demultiplexer_1_out4), .Q(register_5_q), .clk(Clock), .clr(Reset));
  Register #(.trigger("falling")) register_6 (
    .D(WriteData), .en(demultiplexer_1_out5), .Q(register_6_q), .clk(Clock), .clr(Reset));
  Register #(.trigger("falling")) register_7 (
    .D(WriteData), .en(demultiplexer_1_out6), .Q(register_7_q), .clk(Clock), .clr(Reset));
  Register #(.trigger("falling")) register_8 (
    .D(WriteData), .en(demultiplexer_1_out7), .Q(register_8_q), .clk(Clock), .clr(Reset));
  Multiplexer #(.select(3), .width(8), .enable("false")) multiplexer_1 (
    .in0(register_1_q), .in1(register_2_q), .in2(register_3_q), .in3(register_4_q), .in4(register_5_q),
    .in5(register_6_q), .in6(register_7_q), .in7(register_8_q), .out(ReadData1), .sel(Read1));
  Multiplexer #(.select(3), .width(8), .enable("false")) multiplexer_2 (
    .in0(register_1_q), .in1(register_2_q), .in2(register_3_q), .in3(register_4_q), .in4(register_5_q),
    .in5(register_6_q), .in6(register_7_q), .in7(register_8_q), .out(ReadData2), .sel(Read2));
endmodule

module controlunit (
  input  [15:0] IR,
  output jump,
  output push,
  output pop,
  output cmp
);

  wire loadi_out, MaybeJump_out;

  and MaybeJump (MaybeJump_out, ~IR[11], IR[12]);  // AND_Gate
  and loadi (loadi_out, ~IR[9], ~IR[10], ~IR[11], IR[12]);  // AND_Gate
  and u_push (push, ~IR[9], ~IR[10], IR[11], IR[12]);  // AND_Gate
  and u_pop (pop, IR[9], ~IR[10], IR[11], IR[12]);  // AND_Gate
  and u_cmp (cmp, ~IR[9], IR[10], IR[11], ~IR[12]);  // AND_Gate
  and YesJump (jump, MaybeJump_out, ~loadi_out);  // AND_Gate
endmodule
