// Logisim project basic.circ as structural Verilog: 4 circuits, main circuit main
module main (
  input  A,
  input  B,
  input  [3:0] A_2,
  input  [3:0] B_2,
  output A_AND_B,
  output A_OR_B,
  output NOT_A,
  output [3:0] A_AND_B_2,
  output [3:0] A_OR_B_2,
  output [3:0] NOT_A_2
);

  and and_1 (A_AND_B, A, B);
  or or_1 (A_OR_B, A, B);
  not not_1 (NOT_A, A);
  assign A_AND_B_2 = A_2 & B_2;  // AND_Gate and_2, 4 bits wide
  assign A_OR_B_2 = A_2 | B_2;  // OR_Gate or_2, 4 bits wide
  assign NOT_A_2 = ~A_2;  // NOT_Gate not_2, 4 bits wide
endmodule

module halfadder (
  input  A,
  input  B,
  output Sum,
  output Carryout
);

  wire and_1_out, and_2_out;

  and and_1 (and_1_out, ~A, B);  // AND_Gate
  or or_1 (Sum, and_1_out, and_2_out);
  and and_2 (and_2_out, A, ~B);  // AND_Gate
  and and_3 (Carryout, A, B);
endmodule

module fulladder (
  input  A,
  input  B,
  input  C_in,
  output Sum,
  output C_out
);

  wire and_1_out, and_2_out, and_3_out, and_4_out, and_5_out, and_6_out, and_7_out;

  and and_1 (and_1_out, ~A, ~B, C_in);  // AND_Gate
  and and_2 (and_2_out, ~A, B, ~C_in);  // AND_Gate
  and and_3 (and_3_out, A, ~B, ~C_in);  // AND_Gate
  and and_4 (and_4_out, A, B, C_in);
  and and_5 (and_5_out, A, B, ~C_in);  // AND_Gate
  and and_6 (and_6_out, A, ~B, C_in);  // AND_Gate
  and and_7 (and_7_out, ~A, B, C_in);  // AND_Gate
  or or_1 (Sum, and_1_out, and_2_out, and_3_out, and_4_out);
  or or_2 (C_out, and_4_out, and_5_out, and_6_out, and_7_out);
endmodule

module _8bitadder (
  input  [7:0] A,
  input  [7:0] B,
  output [7:0] out_3
);

  wire bit0_c_out, bit1_c_out;

  fulladder bit0 (.A(A[0]), .B(B[0]), .C_in(1'b0), .Sum(out_3[0]), .C_out(bit0_c_out));
  fulladder bit1 (.A(A[1]), .B(B[1]), .C_in(bit0_c_out), .C_out(bit1_c_out));  // open: Sum
  fulladder bit2 (.A(A[2]), .B(B[2]), .C_in(bit1_c_out));  // open: Sum, C_out
  fulladder fulladder_1 (.A(A[3]), .B(B[3]));  // open: C_in, Sum, C_out
  fulladder fulladder_2 (.A(A[4]), .B(B[4]));  // open: C_in, Sum, C_out
  fulladder fulladder_3 (.A(A[5]), .B(B[5]));  // open: C_in, Sum, C_out
  fulladder fulladder_4 (.A(A[6]), .B(B[6]));  // open: C_in, Sum, C_out
  fulladder fulladder_5 (.A(A[7]), .B(B[7]));  // open: C_in, Sum, C_out
endmodule
