// Logisim project cachemem-sol2.circ as structural Verilog: 2 circuits, main circuit main
module main (
  output [7:0] dataout,
  output [7:0] hitcount,
  output [7:0] misscount
);

  wire button_1_out, clock_1_out, memorysystem_1_ready, not_1_out;
  wire [7:0] counter_1_q;
  wire [15:0] rom_1_data;

  Clock clock_1 (.out(clock_1_out));
  Button button_1 (.out(button_1_out));
  Counter counter_1 (
    .count(memorysystem_1_ready), .Q(counter_1_q), .clk(clock_1_out), .clr(button_1_out));  // open: load, D, carry
  ROM #(.dataWidth(16)) rom_1 (.addr(counter_1_q), .data(rom_1_data), .sel(1'b1));
  memorysystem memorysystem_1 (
    .addr({4'b0000, rom_1_data[11:0]}), .datain(rom_1_data[14:12]), .Clock(clock_1_out),
    .Write(rom_1_data[15]), .Read(not_1_out), .Reset(button_1_out), .dataout(dataout),
    .ready(memorysystem_1_ready), .HitCount(hitcount), .MissCount(misscount));
  not not_1 (not_1_out, rom_1_data[15]);
  Hex_Digit_Display hex_digit_display_1 (.value(dataout[7:4]));  // open: dp
  Hex_Digit_Display hex_digit_display_2 (.value(dataout[3:0]));  // open: dp
  Hex_Digit_Display hex_digit_display_3 (.value(hitcount[7:4]));  // open: dp
  Hex_Digit_Display hex_digit_display_4 (.value(hitcount[3:0]));  // open: dp
  Hex_Digit_Display hex_digit_display_5 (.value(misscount[7:4]));  // open: dp
  Hex_Digit_Display hex_digit_display_6 (.value(misscount[3:0]));  // open: dp

  // Notes on the sheet:
  //   Fake instructions
  //   R/W bit plus mem addresses
  //   Leading bit... 0=R, 1=W
  //   contents of rom_1 (hex, n*v repeats v):
  //   2000 2001 3002 3003 4004 4005 5006 5007 8000 8001 9002 9003 a004 a005 b006 b007
endmodule

module memorysystem (
  input  [15:0] addr,
  input  [2:0] datain,
  input  Clock,
  input  Write,
  input  Read,
  input  Reset,
  output [7:0] dataout,
  output ready,
  output [7:0] HitCount,
  output [7:0] MissCount
);

  wire and_1_out, and_3_out, and_4_out, and_6_out, and_7_out, and_8_out, and_9_out, comparator_1_eq,
       comparator_2_eq, Hit, MC, MODE_q, not_1_out, not_2_out, not_3_out, NW, or_1_out, SMC;
  wire [3:0] BC;
  wire [7:0] ram_4_data, shift_register_1_q0, shift_register_1_q1, shift_register_1_q2, shift_register_1_q3;
  wire [10:0] ram_1_data;
  wire [15:0] multiplexer_1_out;
  wire [31:0] multiplexer_2_out, ram_2_data, ram_3_data, ram_5_data, ram_6_data;

  Comparator #(.width(4)) comparator_1 (.a(BC), .b(4'b0000), .eq(comparator_1_eq));  // open: gt, lt
  and and_1 (and_1_out, Hit, not_2_out);
  and and_2 (MC, not_3_out, ~Write, not_2_out);  // AND_Gate
  or or_1 (or_1_out, Write, not_1_out);
  not not_1 (not_1_out, comparator_1_eq);
  and and_3 (and_3_out, comparator_1_eq, Clock);
  not not_2 (not_2_out, MODE_q);
  and and_4 (and_4_out, not_3_out, ~Write);  // AND_Gate
  RAM #(.addrWidth(2), .dataWidth(11), .bus("separate")) ram_1 (
    .addr(addr[5:4]), .din({NW, addr[15:6]}), .data(ram_1_data), .str(or_1_out), .sel(1'b1), .clk(Clock),
    .ld(comparator_1_eq), .clr(Reset));
  Counter #(.trigger("falling")) HitCounter (
    .count(and_1_out), .Q(HitCount), .clk(and_3_out), .clr(Reset));  // open: load, D, carry
  not not_3 (not_3_out, Hit);
  and HitDetector (Hit, ram_1_data[10], comparator_1_eq, comparator_2_eq);
  Register #(.width(1), .trigger("falling")) MODE (.D(and_4_out), .en(1'b1), .Q(MODE_q), .clk(Clock), .clr(Reset));
  and and_5 (SMC, MODE_q, Clock);
  and and_6 (and_6_out, ~BC[2], ~BC[3], or_1_out);  // AND_Gate
  Counter #(.trigger("falling")) MissCounter (
    .count(MC), .Q(MissCount), .clk(and_3_out), .clr(Reset));  // open: load, D, carry
  Comparator #(.width(10)) comparator_2 (.a(ram_1_data[9:0]), .b(addr[15:6]), .eq(comparator_2_eq));  // open: gt, lt
  not not_4 (NW, Write);
  RAM #(.addrWidth(2), .dataWidth(32), .bus("separate")) ram_2 (
    .addr(addr[5:4]),
    .din({shift_register_1_q0, shift_register_1_q1, shift_register_1_q2, shift_register_1_q3}),
    .data(ram_2_data), .str(and_6_out), .sel(1'b1), .clk(Clock), .ld(Hit), .clr(Reset));
  Multiplexer #(.width(16), .enable("false")) multiplexer_1 (
    .in0({addr[15:4], BC}), .in1(addr), .out(multiplexer_1_out), .sel(Write));
  and and_7 (and_7_out, BC[2], ~BC[3], or_1_out);  // AND_Gate
  Counter #(.width(4), .max('hf)) counter_1 (.Q(BC), .clk(SMC), .clr(Reset));  // open: load, D, count, carry
  RAM #(.addrWidth(2), .dataWidth(32), .bus("separate")) ram_3 (
    .addr(addr[5:4]),
    .din({shift_register_1_q0, shift_register_1_q1, shift_register_1_q2, shift_register_1_q3}),
    .data(ram_3_data), .str(and_7_out), .sel(1'b1), .clk(Clock), .ld(Hit), .clr(Reset));
  RAM #(.addrWidth(16), .bus("separate")) ram_4 (
    .addr(multiplexer_1_out), .din({{5{1'b0}}, datain}), .data(ram_4_data), .str(Write), .sel(1'b1),
    .clk(Clock), .ld(Read));  // open: clr
  Shift_Register #(.width(8), .length(4), .trigger("falling")) shift_register_1 (
    .shift(1'b1), .in(ram_4_data), .clk(Clock), .clr(Reset), .q0(shift_register_1_q0),
    .q1(shift_register_1_q1), .q2(shift_register_1_q2), .q3(shift_register_1_q3));  // open: out, load, d0, d1, d2, d3
  and and_8 (and_8_out, ~BC[2], BC[3], or_1_out);  // AND_Gate
  RAM #(.addrWidth(2), .dataWidth(32), .bus("separate")) ram_5 (
    .addr(addr[5:4]),
    .din({shift_register_1_q0, shift_register_1_q1, shift_register_1_q2, shift_register_1_q3}),
    .data(ram_5_data), .str(and_8_out), .sel(1'b1), .clk(Clock), .ld(Hit), .clr(Reset));
  and and_9 (and_9_out, BC[2], BC[3], or_1_out);
  RAM #(.addrWidth(2), .dataWidth(32), .bus("separate")) ram_6 (
    .addr(addr[5:4]),
    .din({shift_register_1_q0, shift_register_1_q1, shift_register_1_q2, shift_register_1_q3}),
    .data(ram_6_data), .str(and_9_out), .sel(1'b1), .clk(Clock), .ld(Hit), .clr(Reset));
  Multiplexer #(.select(2), .width(32), .enable("false")) multiplexer_2 (
    .in0(ram_2_data), .in1(ram_3_data), .in2(ram_5_data), .in3(ram_6_data), .out(multiplexer_2_out),
    .sel(addr[3:2]));
  Multiplexer #(.select(2), .width(8), .enable("false")) multiplexer_3 (
    .in0(multiplexer_2_out[7:0]), .in1(multiplexer_2_out[15:8]), .in2(multiplexer_2_out[23:16]),
    .in3(multiplexer_2_out[31:24]), .out(dataout), .sel(addr[1:0]));
  or or_2 (ready, Hit, Write);

  // Other names for the same wires on the sheet: H[7:0] = HitCount; M[7:0] = MissCount; W = Write

  // Notes on the sheet:
  //   Metadata (tag and valid bits)
  //   Cache with block size of 16 bytes and a tiny one at that with only FOUR cache lines
  //   RAM
endmodule
