// Logisim project cachemem.circ as structural Verilog: 2 circuits, main circuit main
module main (
  output [7:0] dataout,
  output [7:0] hitcount,
  output [7:0] misscount
);

  wire button_1_out, clock_1_out, memorysystem_1_ready, not_1_out;
  wire [7:0] counter_1_q;
  wire [15:0] rom_1_data;

  Clock clock_1 (.out(clock_1_out));
  Button button_1 (.out(button_1_out));
  Counter counter_1 (
    .count(memorysystem_1_ready), .Q(counter_1_q), .clk(clock_1_out), .clr(button_1_out));  // open: load, D, carry
  ROM #(.dataWidth(16)) rom_1 (.addr(counter_1_q), .data(rom_1_data), .sel(1'b1));
  memorysystem memorysystem_1 (
    .addr({4'b0000, rom_1_data[11:0]}), .datain(rom_1_data[14:12]), .Clock(clock_1_out),
    .Write(rom_1_data[15]), .Read(not_1_out), .Reset(button_1_out), .dataout(dataout),
    .ready(memorysystem_1_ready), .HitCount(hitcount), .MissCount(misscount));
  not not_1 (not_1_out, rom_1_data[15]);
  Hex_Digit_Display hex_digit_display_1 (.value(dataout[7:4]));  // open: dp
  Hex_Digit_Display hex_digit_display_2 (.value(dataout[3:0]));  // open: dp
  Hex_Digit_Display hex_digit_display_3 (.value(hitcount[7:4]));  // open: dp
  Hex_Digit_Display hex_digit_display_4 (.value(hitcount[3:0]));  // open: dp
  Hex_Digit_Display hex_digit_display_5 (.value(misscount[7:4]));  // open: dp
  Hex_Digit_Display hex_digit_display_6 (.value(misscount[3:0]));  // open: dp

  // Notes on the sheet:
  //   Fake instructions
  //   R/W bit plus mem addresses
  //   Leading bit... 0=R, 1=W
  //   contents of rom_1 (hex, n*v repeats v):
  //   0 1 2 3 4 5 6 7 8008 8009 800a 800b 800c 800d 800e 800f
endmodule

module memorysystem (
  input  [15:0] addr,
  input  [2:0] datain,
  input  Clock,
  input  Write,
  input  Read,
  input  Reset,
  output [7:0] dataout,
  output ready,
  output [7:0] HitCount,
  output [7:0] MissCount
);

  wire and_1_out, and_2_out, and_5_out, and_6_out, and_7_out, and_8_out, comparator_1_eq, comparator_2_eq,
       MC, MODE_q, not_1_out, not_2_out, not_3_out, SMC;
  wire [3:0] BC;
  wire [7:0] ram_4_data;
  wire [10:0] ram_1_data;
  wire [31:0] shift_register_1_q3;

  and and_1 (and_1_out, ready, not_2_out);
  not not_1 (not_1_out, comparator_1_eq);
  Comparator #(.width(4)) comparator_1 (.a(BC), .b(4'b0000), .eq(comparator_1_eq));  // open: gt, lt
  and and_2 (and_2_out, comparator_1_eq, Clock);
  not not_2 (not_2_out, MODE_q);
  and and_3 (MC, not_3_out, not_2_out);
  Counter #(.trigger("falling")) HitCounter (
    .count(and_1_out), .Q(HitCount), .clk(and_2_out), .clr(Reset));  // open: load, D, carry
  not not_3 (not_3_out, ready);
  Register #(.width(1), .trigger("falling")) MODE (.D(not_3_out), .en(1'b1), .Q(MODE_q), .clk(Clock), .clr(Reset));
  RAM #(.addrWidth(2), .dataWidth(11), .bus("separate")) ram_1 (
    .addr(addr[5:4]), .din({1'b1, addr[15:6]}), .data(ram_1_data), .str(not_1_out), .sel(1'b1), .clk(Clock),
    .ld(comparator_1_eq), .clr(Reset));
  Counter #(.trigger("falling")) MissCounter (
    .count(MC), .Q(MissCount), .clk(and_2_out), .clr(Reset));  // open: load, D, carry
  and HitDetector (ready, ram_1_data[10], comparator_1_eq, comparator_2_eq);
  and and_4 (SMC, MODE_q, Clock);
  and and_5 (and_5_out, ~BC[2], ~BC[3]);  // AND_Gate
  RAM #(.addrWidth(2), .dataWidth(32), .bus("separate")) ram_2 (
    .addr(addr[5:4]), .din(shift_register_1_q3), .str(not_1_out), .sel(and_5_out), .clk(Clock), .clr(Reset));  // open: data, ld
  Comparator #(.width(10)) comparator_2 (.a(ram_1_data[9:0]), .b(addr[15:6]), .eq(comparator_2_eq));  // open: gt, lt
  and and_6 (and_6_out, BC[2], ~BC[3]);  // AND_Gate
  RAM #(.addrWidth(2), .dataWidth(32), .bus("separate")) ram_3 (
    .addr(addr[5:4]), .din(shift_register_1_q3), .str(not_1_out), .sel(and_6_out), .clk(Clock), .clr(Reset));  // open: data, ld
  Counter #(.width(4), .max('hf)) counter_1 (.Q(BC), .clk(SMC), .clr(Reset));  // open: load, D, count, carry
  and and_7 (and_7_out, ~BC[2], BC[3]);  // AND_Gate
  Shift_Register #(.width(8), .length(4), .trigger("falling")) shift_register_1 (
    .shift(1'b1), .in(ram_4_data), .clk(Clock), .clr(Reset), .q0(shift_register_1_q3[31:24]),
    .q1(shift_register_1_q3[23:16]), .q2(shift_register_1_q3[15:8]), .q3(shift_register_1_q3[7:0]));  // open: out, load, d0, d1, d2, d3
  RAM #(.addrWidth(16), .bus("separate")) ram_4 (
    .addr({addr[15:4], BC}), .din({{5{1'b0}}, datain}), .data(ram_4_data), .str(Write), .sel(1'b1),
    .clk(Clock), .ld(Read));  // open: clr
  RAM #(.addrWidth(2), .dataWidth(32), .bus("separate")) ram_5 (
    .addr(addr[5:4]), .din(shift_register_1_q3), .str(not_1_out), .sel(and_7_out), .clk(Clock), .clr(Reset));  // open: data, ld
  and and_8 (and_8_out, BC[2], BC[3]);
  RAM #(.addrWidth(2), .dataWidth(32), .bus("separate")) ram_6 (
    .addr(addr[5:4]), .din(shift_register_1_q3), .str(not_1_out), .sel(and_8_out), .clk(Clock), .clr(Reset));  // open: data, ld

  // Other names for the same wires on the sheet: H[7:0] = HitCount; Hit = ready; M[7:0] = MissCount

  // Notes on the sheet:
  //   Metadata (tag and valid bits)
  //   Cache with block size of 16 bytes and a tiny one at that with only FOUR cache lines
  //   RAM
endmodule
