// Logisim project midterm1.circ as structural Verilog: 1 circuit, main circuit main
module main (
  input  A,
  input  B,
  input  C,
  input  [1:0] SELECT,
  input  [3:0] INPUT0,
  input  [3:0] INPUT0_2,
  input  [3:0] INPUT0_3,
  input  [3:0] INPUT0_4,
  output Output,
  output [3:0] Output_2
);

  wire [3:0] multiplexer_1_out;

  and and_1 (Output, A, ~B, ~C);  // AND_Gate
  Multiplexer #(.select(2), .width(4), .enable("false")) multiplexer_1 (
    .in0(INPUT0), .in1(INPUT0_2), .in2(INPUT0_3), .in3(INPUT0_4), .out(multiplexer_1_out), .sel(SELECT));
endmodule
