// Logisim project review.circ as structural Verilog: 2 circuits, main circuit main
module main (
  input  A,
  input  B,
  input  [7:0] in_3,
  input  [7:0] in_4,
  output [7:0] out_5
);

  playground playground_1 (.A(A), .B(B));  // open: out1, out2, out3
  Adder adder_1 (.a(in_3), .b(in_4), .out(out_5));  // open: cin, cout
endmodule

module playground (
  input  A,
  input  B,
  output out1,
  output out2,
  output out3
);

  and and_1 (out1, A, B);
  or or_1 (out2, A, B);
  nand nand_1 (out3, A, B);
endmodule
