// Logisim project x86cpu.circ as structural Verilog: 6 circuits, main circuit main
module main (
);

  wire ALU_equal, and_1_out, and_2_out, Clock_out, cmp, equal, j, je, jne, jump, not_1_out, or_1_out,
       or_2_out, or_3_out, or_4_out, pop, push, Reset_out, W_out;
  wire [1:0] Sel0_out;
  wire [7:0] adder_1_out, adder_2_out, ALU_aluout, bit_extender_1_out, counter_1_q, multiplexer_2_out,
       multiplexer_3_out, PC_q, ram_2_data, RegFile_readdata1, RegFile_readdata2;
  wire [15:0] IR, ram_1_data;

  Multiplexer #(.width(8), .enable("false")) multiplexer_1 ();  // open: in0, in1, out, sel
  Adder adder_1 (.a(PC_q), .b(IR[7:0]), .out(adder_1_out));  // open: cin, cout
  and and_1 (and_1_out, je, equal);
  and and_2 (and_2_out, ~equal, jne);  // AND_Gate
  Counter #(.trigger("falling")) PC (
    .load(or_1_out), .D(adder_1_out), .count(not_1_out), .Q(PC_q), .clk(Clock_out), .clr(Reset_out));  // open: carry
  not not_1 (not_1_out, or_1_out);
  or or_1 (or_1_out, and_1_out, and_2_out, j);
  Clock Clock (.out(Clock_out));
  Multiplexer #(.width(8), .enable("false")) multiplexer_2 (
    .in0(counter_1_q), .in1(adder_2_out), .out(multiplexer_2_out), .sel(pop));
  Adder adder_2 (.a(8'h1), .b(counter_1_q), .out(adder_2_out));  // open: cin, cout
  or or_2 (or_2_out, Reset_out, push);
  or or_3 (or_3_out, push, pop);
  or or_4 (or_4_out, Clock_out, Reset_out);
  RAM #(.dataWidth(16)) ram_1 (.addr(PC_q), .data(ram_1_data), .clk(Clock_out));  // open: sel, ld, clr
  RAM #(.bus("separate")) ram_2 (
    .addr(multiplexer_2_out), .din(RegFile_readdata2), .data(ram_2_data), .str(push), .clk(Clock_out),
    .ld(pop), .clr(Reset_out));  // open: sel
  Counter counter_1 (
    .load(or_2_out), .D({8{1'b1}}), .count(or_3_out), .Q(counter_1_q), .clk(or_4_out));  // open: carry, clr
  Register #(.width(16)) u_IR (.D(ram_1_data), .en(1'b1), .Q(IR), .clk(Clock_out), .clr(Reset_out));
  assign bit_extender_1_out = {{2{IR[5]}}, IR[5:0]};  // Bit_Extender bit_extender_1
  and Sel0 (Sel0_out[0], ~IR[9], IR[12]);  // AND_Gate
  and Sel1 (Sel0_out[1], IR[9], IR[12]);
  controlunit controlunit_1 (.IR(IR), .je(je), .jne(jne), .j(j), .cmp(cmp), .jump(jump), .push(push), .pop(pop));
  Multiplexer #(.select(2), .width(8), .enable("false")) multiplexer_3 (
    .in0(ALU_aluout), .in1(bit_extender_1_out), .in2(ram_2_data), .out(multiplexer_3_out), .sel(Sel0_out));  // open: in3
  and W (W_out, ~jump, ~push);  // AND_Gate
  registerfile RegFile (
    .Read1(IR[5:3]), .Read2(IR[2:0]), .RegWrite(IR[8:6]), .WriteData(multiplexer_3_out), .WE(W_out),
    .Clock(Clock_out), .Reset(Reset_out), .ReadData1(RegFile_readdata1), .ReadData2(RegFile_readdata2));
  Button Reset (.out(Reset_out));
  ALU ALU (.A(RegFile_readdata1), .B(RegFile_readdata2), .Operation(IR[11:9]), .Equal(ALU_equal), .ALUout(ALU_aluout));
  Register #(.width(1), .trigger("falling")) register_1 (
    .D(ALU_equal), .en(cmp), .Q(equal), .clk(Clock_out), .clr(Reset_out));

  // Notes on the sheet:
  //   Instruction cache
  //   Data cache (stack)
endmodule

module playground (
  input  [7:0] A,
  input  [7:0] B,
  input  in_3,
  input  [3:0] in_4,
  input  [1:0] in_5,
  input  [2:0] in_6,
  input  [2:0] in_7,
  input  [2:0] in_8,
  input  [1:0] in_9,
  input  [2:0] in_10,
  input  [7:0] Input00,
  input  [7:0] Input01,
  input  [7:0] Input10,
  input  [7:0] Input11,
  output [7:0] A_plus_B,
  output out_16,
  output [7:0] Memout,
  output [2:0] out_18,
  output [7:0] out_19
);

  wire button_1_out, clock_1_out;

  Adder adder_1 (.a(A), .b(B), .out(A_plus_B));  // open: cin, cout
  Hex_Digit_Display hex_digit_display_1 (.value(in_4));  // open: dp
  Multiplexer #(.select(2), .width(8), .enable("false")) multiplexer_1 (
    .in0(Input00), .in1(Input01), .in2(Input10), .in3(Input11), .out(out_19), .sel(in_9));
  Hex_Digit_Display hex_digit_display_2 (.value(A_plus_B[7:4]));  // open: dp
  Register register_1 (.D(A_plus_B), .en(1'b1), .Q(Memout), .clk(clock_1_out));  // open: clr
  Clock clock_1 (.out(clock_1_out));
  Hex_Digit_Display hex_digit_display_3 (.value(A_plus_B[3:0]));  // open: dp
  Hex_Digit_Display hex_digit_display_4 (.value(Memout[7:4]));  // open: dp
  memory memory_1 (.D(in_3), .WE(button_1_out), .CurrentValue(out_16));
  Button button_1 (.out(button_1_out));
  Hex_Digit_Display hex_digit_display_5 (.value(Memout[3:0]));  // open: dp
  Multiplexer #(.select(2), .width(3), .enable("false")) multiplexer_2 (
    .in0(in_6), .in1(in_7), .in2(in_8), .in3(in_10), .out(out_18), .sel(in_5));
endmodule

module ALU (
  input  [2:0] Operation,
  input  [7:0] A,
  input  [7:0] B,
  output [7:0] ALUout,
  output Equal
);

  wire [7:0] adder_1_out, and_1_out, nand_out, nor_out, or_1_out, subtractor_1_out;

  Adder adder_1 (.a(A), .b(B), .out(adder_1_out));  // open: cin, cout
  Subtractor subtractor_1 (.a(A), .b(B), .out(subtractor_1_out));  // open: bin, bout
  assign and_1_out = A & B;  // AND_Gate and_1, 8 bits wide
  assign or_1_out = A | B;  // OR_Gate or_1, 8 bits wide
  assign nand_out = ~A | ~B;  // OR_Gate nand, 8 bits wide
  assign nor_out = ~A & ~B;  // AND_Gate nor, 8 bits wide
  Comparator comparator_1 (.a(A), .b(B), .eq(Equal));  // open: gt, lt
  Multiplexer #(.select(3), .width(8), .enable("false")) multiplexer_1 (
    .in0(adder_1_out), .in1(subtractor_1_out), .in2(and_1_out), .in3(or_1_out), .in4(nand_out),
    .in5(nor_out), .in6({{7{1'b0}}, Equal}), .out(ALUout), .sel(Operation));  // open: in7
endmodule

module memory (
  input  D,
  input  WE,
  output CurrentValue
);

  wire nand_1_out, nand_2_out, nand_4_out;

  nand nand_1 (nand_1_out, D, WE);
  nand nand_2 (nand_2_out, WE, ~D);  // NAND_Gate
  nand nand_3 (CurrentValue, nand_1_out, nand_4_out);
  nand nand_4 (nand_4_out, CurrentValue, nand_2_out);
endmodule

module registerfile (
  input  [2:0] Read1,
  input  [2:0] Read2,
  input  [2:0] RegWrite,
  input  [7:0] WriteData,
  input  WE,
  input  Clock,
  input  Reset,
  output [7:0] ReadData1,
  output [7:0] ReadData2
);

  wire demultiplexer_1_out0, demultiplexer_1_out1, demultiplexer_1_out2, demultiplexer_1_out3,
       demultiplexer_1_out4, demultiplexer_1_out5, demultiplexer_1_out6, demultiplexer_1_out7;
  wire [7:0] register_1_q, register_2_q, register_3_q, register_4_q, register_5_q, register_6_q,
       register_7_q, register_8_q;

  Demultiplexer #(.select(3), .enable("false")) demultiplexer_1 (
    .out0(demultiplexer_1_out0), .out1(demultiplexer_1_out1), .out2(demultiplexer_1_out2),
    .out3(demultiplexer_1_out3), .out4(demultiplexer_1_out4), .out5(demultiplexer_1_out5),
    .out6(demultiplexer_1_out6), .out7(demultiplexer_1_out7), .in(WE), .sel(RegWrite));
  Register #(.trigger("falling")) register_1 (
    .D(WriteData), .en(demultiplexer_1_out0), .Q(register_1_q), .clk(Clock), .clr(Reset));
  Register #(.trigger("falling")) register_2 (
    .D(WriteData), .en(demultiplexer_1_out1), .Q(register_2_q), .clk(Clock), .clr(Reset));
  Register #(.trigger("falling")) register_3 (
    .D(WriteData), .en(demultiplexer_1_out2), .Q(register_3_q), .clk(Clock), .clr(Reset));
  Register #(.trigger("falling")) register_4 (
    .D(WriteData), .en(demultiplexer_1_out3), .Q(register_4_q), .clk(Clock), .clr(Reset));
  Register #(.trigger("falling")) register_5 (
    .D(WriteData), .en(demultiplexer_1_out4), .Q(register_5_q), .clk(Clock), .clr(Reset));
  Register #(.trigger("falling")) register_6 (
    .D(WriteData), .en(demultiplexer_1_out5), .Q(register_6_q), .clk(Clock), .clr(Reset));
  Register #(.trigger("falling")) register_7 (
    .D(WriteData), .en(demultiplexer_1_out6), .Q(register_7_q), .clk(Clock), .clr(Reset));
  Register #(.trigger("falling")) register_8 (
    .D(WriteData), .en(demultiplexer_1_out7), .Q(register_8_q), .clk(Clock), .clr(Reset));
  Multiplexer #(.select(3), .width(8), .enable("false")) multiplexer_1 (
    .in0(register_1_q), .in1(register_2_q), .in2(register_3_q), .in3(register_4_q), .in4(register_5_q),
    .in5(register_6_q), .in6(register_7_q), .in7(register_8_q), .out(ReadData1), .sel(Read1));
  Multiplexer #(.select(3), .width(8), .enable("false")) multiplexer_2 (
    .in0(register_1_q), .in1(register_2_q), .in2(register_3_q), .in3(register_4_q), .in4(register_5_q),
    .in5(register_6_q), .in6(register_7_q), .in7(register_8_q), .out(ReadData2), .sel(Read2));
endmodule

module controlunit (
  input  [15:0] IR,
  output jump,
  output push,
  output pop,
  output cmp,
  output j,
  output je,
  output jne
);

  wire loadi_out, MaybeJump_out;

  and MaybeJump (MaybeJump_out, ~IR[11], IR[12]);  // AND_Gate
  and loadi (loadi_out, ~IR[9], ~IR[10], ~IR[11], IR[12]);  // AND_Gate
  and u_push (push, ~IR[9], ~IR[10], IR[11], IR[12]);  // AND_Gate
  and u_pop (pop, IR[9], ~IR[10], IR[11], IR[12]);  // AND_Gate
  and u_cmp (cmp, ~IR[9], IR[10], IR[11], ~IR[12]);  // AND_Gate
  and u_j (j, IR[9], ~IR[10], ~IR[11], IR[12]);  // AND_Gate
  and u_je (je, ~IR[9], IR[10], ~IR[11], IR[12]);  // AND_Gate
  and u_jne (jne, IR[9], IR[10], ~IR[11], IR[12]);  // AND_Gate
  and YesJump (jump, MaybeJump_out, ~loadi_out);  // AND_Gate
endmodule
